# Fritzing sketch Sketch (saved by Fritzing 0.9.3b)
circuit board: 5.28145cm x 5.18941cm
breadboards: 1

parts:
  Arduino_Nano = Arduino Nano (Rev3.0)
  Power_Input_12V = Screw terminal - 2 pins [package=THT]
  QG = Basic FET N-Channel [part_number=IRLB8721 package="TO220 [THT]"]
  QB = Basic FET N-Channel [part_number=IRLB8721 package="TO220 [THT]"]
  QR = Basic FET N-Channel [part_number=IRLB8721 package="TO220 [THT]"]
  R0 = female pin header, 1 pin [form="♀ (female)"]
  G0 = female pin header, 1 pin [form="♀ (female)"]
  B0 = female pin header, 1 pin [form="♀ (female)"]
  W0 = female pin header, 1 pin [form="♀ (female)"]
  W1 = female pin header, 1 pin [form="♀ (female)"]
  G1 = female pin header, 1 pin [form="♀ (female)"]
  R1 = female pin header, 1 pin [form="♀ (female)"]
  B1 = female pin header, 1 pin [form="♀ (female)"]
  W2 = female pin header, 1 pin [form="♀ (female)"]
  G2 = female pin header, 1 pin [form="♀ (female)"]
  R2 = female pin header, 1 pin [form="♀ (female)"]
  B2 = female pin header, 1 pin [form="♀ (female)"]
  W3 = female pin header, 1 pin [form="♀ (female)"]
  G3 = female pin header, 1 pin [form="♀ (female)"]
  B3 = female pin header, 1 pin [form="♀ (female)"]
  R3 = female pin header, 1 pin [form="♀ (female)"]

nets:
  GND: Arduino_Nano.GND, Power_Input_12V.pin2, QG.source, QB.source, QR.source
  N1: Arduino_Nano.D3, QB.gate
  N2: Arduino_Nano.D5, QR.gate
  N3: Arduino_Nano.D6, QG.gate
  12V: Arduino_Nano.VIN, Power_Input_12V.pin1, W0.pin1, W1.pin1, W2.pin1, W3.pin1
  N4: QG.drain, G0.pin1, G1.pin1, G2.pin1, G3.pin1
  N5: QB.drain, B0.pin1, B1.pin1, B2.pin1, B3.pin1
  N6: QR.drain, R0.pin1, R1.pin1, R2.pin1, R3.pin1

notes:
  12V
  GND
  rgbCase
  V1.0
  http://www.lightgraffiti.de

// code stored in the sketch: arduino.ino
/// Serial message protocol
/// =======================
///
/// Each message contains of 6 byte.
///
/// Start Byte | Type Byte | Data Byte 0 | Data Byte 1 | Data Byte 2 | End Byte
/// 0x0f       | 0x..      | 0x..        | 0x..        | 0x..        | 0xff
///
/// Message         | Type Byte | Data Byte 0 | Data Byte 1 | Data Byte 2
/// Heart Beat Req. | 0x00      | 0x00        | 0x00        | 0x00
/// Heart Beat Ack. | 0x01      | 0x00        | 0x00        | 0x00
/// Brightness Req. | 0x02      | value       | 0x00        | 0x00
/// Brightness Ack. | 0x03      | value       | 0x00        | 0x00
/// Mode Req.       | 0x04      | value       | param 0     | param 1
/// Mode Ack.       | 0x05      | value       | param 0     | param 1
/// Color Req.      | 0x06      | red         | green       | blue
/// Color Ack.      | 0x07      | red         | green       | blue
/// Error           | 0xff      | err code 0  | err code 1  | err code 2

#define GAMMA_CORRECTION

#include <avr/io.h> 
#include <avr/wdt.h>
#include <EEPROM.h>

#ifdef GAMMA_CORRECTION
const uint8_t PROGMEM gamma8[] = {
    0,  0,  0,  0,  0,  0,  0,  0,  0,  0,  0,  0,  0,  0,  0,  0,
    0,  0,  0,  0,  0,  0,  0,  0,  0,  0,  0,  0,  1,  1,  1,  1,
    1,  1,  1,  1,  1,  1,  1,  1,  1,  2,  2,  2,  2,  2,  2,  2,
    2,  3,  3,  3,  3,  3,  3,  3,  4,  4,  4,  4,  4,  5,  5,  5,
    5,  6,  6,  6,  6,  7,  7,  7,  7,  8,  8,  8,  9,  9,  9, 10,
   10, 10, 11, 11, 11, 12, 12, 13, 13, 13, 14, 14, 15, 15, 16, 16,
   17, 17, 18, 18, 19, 19, 20, 20, 21, 21, 22, 22, 23, 24, 24, 25,
   25, 26, 27, 27, 28, 29, 29, 30, 31, 32, 32, 33, 34, 35, 35, 36,
   37, 38, 39, 39, 40, 41, 42, 43, 44, 45, 46, 47, 48, 49, 50, 50,
   51, 52, 54, 55, 56, 57, 58, 59, 60, 61, 62, 63, 64, 66, 67, 68,
   69, 70, 72, 73, 74, 75, 77, 78, 79, 81, 82, 83, 85, 86, 87, 89,
   90, 92, 93, 95, 96, 98, 99,101,102,104,105,107,109,110,112,114,
  115,117,119,120,122,124,126,127,129,131,133,135,137,138,140,142,
  144,146,148,150,152,154,156,158,160,162,164,167,169,171,173,175,
  177,180,182,184,186,189,191,193,196,198,200,203,205,208,210,213,
  215,218,220,223,225,228,231,233,236,239,241,244,247,249,252,255 };
#endif // GAMMA_CORRECTION

//Setup Output
#define ledPin_r 5
#define ledPin_g 6
#define ledPin_b 3

int inputByte_0 = 0;
int inputByte_1 = 0;
int inputByte_2 = 0;
int inputByte_3 = 0;
int inputByte_4 = 0;
int inputByte_5 = 0;

byte brightness = 196;
byte red = 255;
byte green = 0;
byte blue = 0;
byte mode = 0;  // 0: PC send; 1: Breathing; 2: Color Circle; 3: Breathing Circle
byte mode_p0 = 0; // breating: delay; Color Circle: delay; Breathing Circle: delay
byte mode_p1 = 0; // breating: minBrightness; Color Circle: 0; Breathing Circle: minBrightness

bool mode_forward = true;

const int serialReadTimeout_us = 25;

unsigned long lastCmd;
unsigned long lastEEPROM;

//Setup
void setup()
{  
  pinMode(ledPin_r, OUTPUT);
  pinMode(ledPin_g, OUTPUT);
  pinMode(ledPin_b, OUTPUT);
  
  Serial.begin(115200);
  
  lastCmd = millis();
  lastEEPROM = millis();
  
  ReadEEPROM();
}

//Main Loop
void loop()
{
  // Handling messages has highest priority
  HandleBuffer();

  switch(mode)
  {
    case 1: Breathing(); break;
    case 2: ColorCircle(); break;
    case 3: BreathingCircle(); break;
  }
  
  SetColor(brightness, red, green, blue);

  unsigned long duration_ms = millis() - lastEEPROM;
  if(duration_ms >= 900000 || duration_ms < 0)
    WriteEEPROM();
}

bool HasToChangeMode(byte vmin, byte vmax, bool forward)
{
  return ((brightness <= mode_p1 && !forward) || (brightness >= 255 && forward));
}

void Breathing()
{
  if (HasToChangeMode(mode_p1, 255, mode_forward))
      mode_forward = !mode_forward;
  brightness = (byte)((int)brightness + (mode_forward ? 1 : -1));
  if (mode_p0 < 2)
    mode_p0 = 2;
  delay(mode_p0);
}

void ColorCircle_Init()
{
    red = 0;
    green = 0;
    blue = 0;
    if (brightness < 10)
        brightness = 255;
    mode_p1 = 0;
}

void ColorCircle()
{
  switch (mode_p1)
  {
      case 0:
          if (red >= 254) mode_p1 = 1;
          ++red;
          break;
      case 1:
          if (blue >= 254) mode_p1 = 2;
          ++blue;
          break;
      case 2:
          if (green >= 254) mode_p1 = 3;
          ++green;
          break;
      case 3:
          if (red <= 1) mode_p1 = 4;
          --red;
          break;
      case 4:
          if (blue <= 1) mode_p1 = 5;
          --blue;
          break;
      case 5:
          if (green <= 1) mode_p1 = 0;
          --green;
          break;
  }
  if (mode_p0 < 2)
    mode_p0 = 2;
  delay(mode_p0);
}

void BreathingCircle_Init()
{
    red = (byte)random(255);
    green = (byte)random(255);
    blue = (byte)random(255);
    if (brightness < 10)
        brightness = 255;
    mode_p1 = 0;
}

void BreathingCircle()
{
  if (HasToChangeMode(mode_p1, 255, mode_forward))
      mode_forward = !mode_forward;

  if (brightness <= mode_p1)
  {
    red = (byte)random(255);
    green = (byte)random(255);
    blue = (byte)random(255);
  }
      
  brightness = (byte)((int)brightness + (mode_forward ? 1 : -1));
  if (mode_p0 < 2)
    mode_p0 = 2;
  delay(mode_p0);
}

void(* resetFunc) (void) = 0; //declare reset function @ address 0

bool HandleBuffer()
{
  if (Serial.available() >= 6)
  {
    while(inputByte_0 == 0 && Serial.peek() != 0x0f)
      Serial.read();
      
    //Read buffer
    inputByte_0 = Serial.read();
    delayMicroseconds(serialReadTimeout_us);
    inputByte_1 = Serial.read();
    delayMicroseconds(serialReadTimeout_us);
    inputByte_2 = Serial.read();
    delayMicroseconds(serialReadTimeout_us);
    inputByte_3 = Serial.read();
    delayMicroseconds(serialReadTimeout_us);
    inputByte_4 = Serial.read();
    delayMicroseconds(serialReadTimeout_us);
    inputByte_5 = Serial.read();
  }

  //Check for start of Message
  if (inputByte_0 == 0x0f && inputByte_5 == 0xff)
  {    
    //Detect Command type
    switch (inputByte_1)
    {
      case 0x00: // Heart beat
        Send(0x01, 0x00, 0x00, 0x00);
        break;
      case 0x02: // Brightness
        brightness = inputByte_2;
        Send(0x03, brightness, 0x00, 0x00);
        break;
      case 0x04: // Mode
        mode = inputByte_2;
        mode_p0 = inputByte_3;
        mode_p1 = inputByte_4;
        Send(0x05, mode, 0x00, 0x00);
        switch(mode)
        {
          case 2: ColorCircle_Init(); break;
          case 3: BreathingCircle_Init(); break;
        }
        WriteEEPROM();
        break;
      case 0x06: // Color
        red = inputByte_2;
        green = inputByte_3;
        blue = inputByte_4;
        Send(0x07, red, green, blue);
        break;
    }
    lastCmd = millis();

    inputByte_0 = 0;
    inputByte_1 = 0;
    inputByte_2 = 0;
    inputByte_3 = 0;
    inputByte_4 = 0;
    inputByte_5 = 0;
  }
  else if(millis() - lastCmd > 360000)
  {
    Send(0xff, 0x0f, 0x0f, 0x0f);
    wdt_enable(WDTO_1S);
  }
}

static void SetColor(int brightness, int red, int green, int blue)
{
#ifdef GAMMA_CORRECTION
  analogWrite(ledPin_r, pgm_read_byte_near(&gamma8[red  ]) * brightness / 255);
  analogWrite(ledPin_g, pgm_read_byte_near(&gamma8[green]) * brightness / 255);
  analogWrite(ledPin_b, pgm_read_byte_near(&gamma8[blue ]) * brightness / 255);
#else // GAMMA_CORRECTION
  analogWrite(ledPin_r, red   * brightness / 255));
  analogWrite(ledPin_g, green * brightness / 255));
  analogWrite(ledPin_b, blue  * brightness / 255));
#endif // GAMMA_CORRECTION
}

static void Send(byte bType, byte bD0, byte bD1, byte bD2)
{
  byte buf[6];
  buf[0] = 0x0f;
  buf[1] = bType;
  buf[2] = bD0;
  buf[3] = bD1;
  buf[4] = bD2;
  buf[5] = 0xff;
  Serial.write(buf, 6);
}

void WriteEEPROM()
{
  EEPROM.write(0, brightness);
  EEPROM.write(1, red);
  EEPROM.write(2, green);
  EEPROM.write(3, blue);
  EEPROM.write(4, mode);
  EEPROM.write(5, mode_p0);
  EEPROM.write(6, mode_p1);
}

void ReadEEPROM()
{
  brightness = EEPROM.read(0);
  red = EEPROM.read(1);
  green = EEPROM.read(2);
  blue = EEPROM.read(3);
  mode = EEPROM.read(4);
  mode_p0 = EEPROM.read(5);
  mode_p1 = EEPROM.read(6);
}
